# Fritzing sketch baki (saved by Fritzing 0.9.3b)
circuit board: 31.4098cm x 21.1458cm
breadboards: 2

parts:
  Raspberry_Pi_1 = Raspberry Pi 3 [part_number=RPI-3-V1.2]
  METER1 = 7-Segment Panel Voltmeter
  Part1 = Adafruit 16-Channel PWM + Servo HAT [part_number="Adafruit #2327"]
  M3 = DC Motor
  BATT1 = LiPoly Battery (1300mAh)
  M5 = DC Motor
  U1 = LCD-16X2 [package=lcd-16x2_noholes]
  Part2 = Adafruit I2C+SPI LCD Backpack [part_number="Adafruit #292"]
  U3 = SWITCH-SPST-2 [package=switch-spst-vertical]
  U4 = DIODE-ZENER [package=diode-zener]
  U5 = SWITCH-SPST-2 [package=switch-spst-vertical]
  R1 = Resistor [tolerance=±5% resistance=10k package=THT]
  LED1 = LEDs [package=led-0603]
  M2 = DC Motor
  Q1 = Basic FET N-Channel [package="D2Pak [SMD]"]
  LED2 = LEDs [package=led-0603]
  Q2 = Basic FET N-Channel [package="D2Pak [SMD]"]
  R2 = Resistor [tolerance=±5% resistance=10k package=THT]
  M4 = RioRand LM2596
  J1 = Basic Servo
  J2 = Basic Servo
  Q3 = Basic FET N-Channel [package="D2Pak [SMD]"]
  Q4 = Basic FET N-Channel [package="D2Pak [SMD]"]
  R3 = Resistor [tolerance=±5% resistance=10k package="2010 [SMD]"]
  R4 = Resistor [tolerance=±5% resistance=10k package="2010 [SMD]"]
  M1 = DC Motor

nets:
  3V3: Raspberry_Pi_1.3v3, Raspberry_Pi_1.3V3, Part1.3.3V
  N1: Raspberry_Pi_1.GPIO2, Part1.SDA, Part2.DATA
  N2: Raspberry_Pi_1.GPIO3, Part1.SCL, Part2.CLOCK
  N3: Raspberry_Pi_1.GIPO4, Part1.GPIO4
  GND: Raspberry_Pi_1.GND, Part1.GND, U1.DB5, U1.K, Part2.GND, U4.A, M4.Pin_4, J1.gnd, J2.gnd, Q3.source, Q4.source, R3.Pin_0, R4.Pin_1
  N4: Raspberry_Pi_1.GIPO17, Part1.GPIO17, Q4.Gate, R3.Pin_1
  N5: Raspberry_Pi_1.GIPO27, Part1.GPIO27
  N6: Raspberry_Pi_1.GIPO22, Part1.GPIO22
  N7: Raspberry_Pi_1.GIPO10, Part1.SPI_MOSI
  N8: Raspberry_Pi_1.GIPO9, Part1.SPI_MISO
  N9: Raspberry_Pi_1.GIPO11, Part1.SPI_SCLK
  N10: Raspberry_Pi_1.ID_SD, Part1.EEDATA
  N11: Raspberry_Pi_1.GIPO5, Part1.GPIO5
  N12: Raspberry_Pi_1.GIPO6, Part1.GPIO6
  N13: Raspberry_Pi_1.GIPO13, Part1.GPIO13
  N14: Raspberry_Pi_1.GIPO19, Part1.GPIO19
  N15: Raspberry_Pi_1.GIPO26, Part1.GPIO26
  N16: Raspberry_Pi_1.GIPO21, Part1.GPIO21
  N17: Raspberry_Pi_1.GIPO20, Part1.GPIO20
  N18: Raspberry_Pi_1.GIPO16, Part1.GPIO16
  N19: Raspberry_Pi_1.GIPO12, Part1.GPIO12
  N20: Raspberry_Pi_1.ID_SC, Part1.EECLK
  N21: Raspberry_Pi_1.GIPO7, Part1.SPI_CE1
  N22: Raspberry_Pi_1.GIPO8, Part1.SPI_CE0
  N23: Raspberry_Pi_1.GIPO25, Part1.GPIO25
  N24: Raspberry_Pi_1.GIPO24, Part1.GPIO24
  N25: Raspberry_Pi_1.GIPO23, Part1.GPIO23
  N26: Raspberry_Pi_1.GIPO18, Part1.GPIO18, Q3.Gate, R4.Pin_0
  N27: Raspberry_Pi_1.GIPO15, Part1.RXD
  N28: Raspberry_Pi_1.GIPO14, Part1.TXD
  5V: Raspberry_Pi_1.5V, Part1.5.0V, U1.VDD, U1.A, Part2.VCC, M4.Pin_3
  N29: METER1.V+, M3.pin_1, BATT1.positive, M5.pin_2, U3.P, U4.C, U5.P, LED1.C, M2.pin_1, LED2.C, M4.Pin_1, M1.pin_2
  N30: METER1.V-, Q2.drain, M4.Pin_2
  N31: Part1.#4, J2.pulse
  VCC: Part1.+5V, J1.vcc, J2.vcc
  N32: Part1.#12, J1.pulse
  N33: M3.pin_2, M5.pin_1, Q4.drain
  N34: BATT1.negative, R1.Pin_1, Q1.source, Q2.source, R2.Pin_1
  N35: U1.VSS, Part2.LEDK
  N36: U1.VO, Part2.DB7
  N37: U1.RS, Part2.DB6
  N38: U1.R_W, Part2.DB5
  N39: U1.E, Part2.DB4
  N40: U1.DB0, Part2.DB3
  N41: U1.DB1, Part2.DB2
  N42: U1.DB2, Part2.DB1
  N43: U1.DB3, Part2.DB0
  N44: U1.DB4, Part2.E
  N45: U1.DB6, Part2.RS
  N46: U1.DB7, Part2.CONTRAST
  N47: U3.O, Q2.Gate, R2.Pin_0
  N48: U5.O, R1.Pin_0, Q1.Gate
  N49: LED1.A, M2.pin_2, Q1.drain, LED2.A
  N50: Q3.drain, M1.pin_1

custom parts:
  7-Segment Panel Voltmeter: 7-Segment Panel Voltmeter (4.5 - 30V)
  Adafruit 16-Channel PWM + Servo HAT: The Raspberry Pi is a wonderful little computer, but one thing it isn't very good at is controlling DC Servo Motors - these motors need very specific and repetitive timing pulses to set the position. Instead of asking the Pi Linux kernel to send these signals, pop on this handy HAT! It adds the capability to control 16 Servos with perfect timing. It can also do PWM up to 1.6 KHz with 12 bit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
  LiPoly Battery (1300mAh): Lithium Ion Polymer Battery (1300mAh)
  Adafruit I2C+SPI LCD Backpack: LCD backpacks reduce the number of pins needed to connect to an LCD. LCDs are a fun and easy way to have your microcontroller project talk back to you. Character LCDs are common, and easy to get, available in tons of colors and sizes. We've written tutorials on using character LCDs with an Arduino (or similar microcontroller) but find that the number of pins necessary to control the LCD can be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
